# Fritzing sketch multiple_board (saved by Fritzing 0.9.3b)

parts:
  Composant1 = Arduino Uno (Rev3) - ICSP
  Composant2 = Arduino Uno (Rev3) - ICSP

nets:
  N1: Composant1.A4/SDA, Composant2.A4/SDA
  N2: Composant1.A5/SCL, Composant2.A5/SCL
  GND: Composant1.GND, Composant2.GND
