# Fritzing sketch potentiometer (saved by Fritzing 0.9.3b)
breadboards: 1

parts:
  Composant1 = Arduino Uno (Rev3)
  U1 = SLIDER [package=slider]

nets (from the breadboard view):
  N1: Composant1.A5/SCL, U1.S
  N2: Composant1.GND, U1.E, U1.A
