# Fritzing sketch push_button (saved by Fritzing 0.9.3b)
breadboards: 1

parts:
  Composant1 = Arduino Uno (Rev3)
  R1 = Resistor [tolerance=±5% resistance=220 package=THT]
  S1 = Pushbutton [package="[SMD]"]

nets:
  N1: Composant1.D8, R1.Pin_1, S1.Pin_3, S1.Pin_4
  N2: Composant1.5V, S1.Pin_1, S1.Pin_2
  N3: Composant1.GND, R1.Pin_0
