# Fritzing sketch rotary_encoder (saved by Fritzing 0.9.3b)
breadboards: 1

parts:
  Composant1 = Arduino Uno (Rev3)
  RE1 = Rotary Encoder [package=THT]
  R1 = Resistor [tolerance=±5% resistance=220 package=THT]
  R2 = Resistor [tolerance=±5% resistance=220 package=THT]

nets:
  N1: Composant1.GND, R1.Pin_0, R2.Pin_1
  N2: Composant1.D5_PWM, RE1.EncoderPinA, R1.Pin_1
  N3: Composant1.D6_PWM, RE1.EncoderPinB, R2.Pin_0
  N4: Composant1.5V, RE1.EncoderPinC
