# Fritzing sketch rotary_switch (saved by Fritzing 0.9.3b)
breadboards: 1

parts:
  Composant1 = Arduino Uno (Rev3)
  switch1 = RM-series Subminiature Rotary Switch
  R1 = Resistor [tolerance=±5% resistance=220 package=THT]
  R2 = Resistor [tolerance=±5% resistance=220 package=THT]
  R3 = Resistor [tolerance=±5% resistance=220 package=THT]
  R4 = Resistor [tolerance=±5% resistance=220 package=THT]
  R5 = Resistor [tolerance=±5% resistance=220 package=THT]
  R6 = Resistor [tolerance=±5% resistance=220 package=THT]

nets:
  N1: Composant1.D7, switch1.0
  N2: Composant1.5V, switch1.7, R6.Pin_1
  N3: Composant1.GND, switch1.1, R1.Pin_0
  N4: switch1.2, R1.Pin_1, R2.Pin_0
  N5: switch1.3, R2.Pin_1, R3.Pin_0
  N6: switch1.4, R3.Pin_1, R4.Pin_0
  N7: switch1.5, R4.Pin_1, R5.Pin_0
  N8: switch1.6, R5.Pin_1, R6.Pin_0
