# Fritzing sketch toggle_switch (saved by Fritzing 0.9.3b)
breadboards: 1

parts:
  Composant1 = Arduino Uno (Rev3)
  R1 = Resistor [tolerance=±5% resistance=220 package=THT]
  S2 = Taiway 100-SP-X-T1 SPDT Miniature Toggle Switch [part_number=100-SP-X-T1-0-0-B1-M2 package=THT]
  S3 = Taiway 100-SP-X-T1 SPDT Miniature Toggle Switch [part_number=100-SP-X-T1-0-0-B1-M2 package=THT]

nets:
  N1: Composant1.GND, R1.Pin_0, S3.L1
  N2: Composant1.D6_PWM, R1.Pin_1, S2.L1
  N3: Composant1.D7, S3.COM
  N4: Composant1.5V, S2.COM, S3.L2
